# Fritzing sketch WeatherStation PCB (saved by Fritzing 0.9.3b)
circuit board: 10cm x 3.5cm
breadboards: 1

parts:
  Moisture = female pin header, 3 pins [form="♀ (female)"]
  C1 = Capacitor [part_number=104 package=cap-pth-small2]
  Arduino_Pro_Mini = Arduino Pro Mini v13
  BAT- = single row smd female pin header, 1 pin [form="♀ (female)"]
  Serial = female pin header, 6 pins [form="♀ (female)"]
  BAT+ = single row smd female pin header, 1 pin [form="♀ (female)"]
  C4 = Capacitor [part_number=104 package=cap-pth-small2]
  Temp = female pin header, 3 pins [form="♀ (female)"]
  C2 = Capacitor [part_number=104 package=cap-pth-small2]
  RainGauge = female pin header, 2 pins [form="♀ (female)"]
  IN+ = single row smd female pin header, 1 pin [form="♀ (female)"]
  NRF24L01+ = NRF24L01+ Breakout Board
  C5 = Capacitor [part_number=104 package=cap-pth-small2]
  Solar = female pin header, 2 pins [form="♀ (female)"]
  Batt = female pin header, 2 pins [form="♀ (female)"]
  IN- = single row smd female pin header, 1 pin [form="♀ (female)"]
  R3 = Resistor [tolerance=±5% resistance=3.9M package=THT]
  R4 = Resistor [tolerance=±5% resistance=421k package=THT]
  R5 = Resistor [tolerance=±5% resistance=11k package=THT]
  R2 = Resistor [tolerance=±5% resistance=421k package=THT]
  R1 = Resistor [tolerance=±5% resistance=3.9M package=THT]
  C3 = Capacitor Polarized [package=cpol-radial-100uf-25v]
  IC1 = LM3480IM4 [package=sot23-3]
  I2C = female pin header, 4 pins [form="♀ (female)"]
  RST = Pushbutton [package="[THT]"]

nets:
  VCC: Moisture.pin1, Arduino_Pro_Mini.VCC, Serial.pin3, Temp.pin1, NRF24L01+.VCC, C5.1, R5.Pin_0, C3.+, IC1.IN, I2C.pin4
  GND: Moisture.pin2, C1.1, Arduino_Pro_Mini.GND, BAT-.pin1, Serial.pin1, Serial.pin2, C4.2, Temp.pin3, C2.1, RainGauge.pin1, NRF24L01+.GND, C5.2, Solar.pin1, Batt.pin2, IN-.pin1, R4.Pin_1, R2.Pin_1, C3.-, IC1.OUT, I2C.pin3, RST.Pin_1, RST.Pin_2
  N1: Moisture.pin3, Arduino_Pro_Mini.A1
  N2: C1.2, Arduino_Pro_Mini.A2, R2.Pin_0, R1.Pin_0
  N3: Arduino_Pro_Mini.DTR, Serial.pin6
  N4: Arduino_Pro_Mini.D0/TX, Serial.pin5
  N5: Arduino_Pro_Mini.D1/RX, Serial.pin4
  N6: Arduino_Pro_Mini.A4, I2C.pin1
  N7: Arduino_Pro_Mini.A5, I2C.pin2
  N8: Arduino_Pro_Mini.RESET, RST.Pin_3, RST.Pin_4
  N9: Arduino_Pro_Mini.A3, C2.2, R3.Pin_1, R4.Pin_0
  N10: Arduino_Pro_Mini.D13/SCK, NRF24L01+.SCK
  N11: Arduino_Pro_Mini.D12/MISO, NRF24L01+.MISO
  N12: Arduino_Pro_Mini.D11_PWM/MOSI, NRF24L01+.MOSI
  N13: Arduino_Pro_Mini.D10_PWM/SS, NRF24L01+.CS
  N14: Arduino_Pro_Mini.D9_PWM, NRF24L01+.CE
  N15: Arduino_Pro_Mini.D4, Temp.pin2, R5.Pin_1
  N16: Arduino_Pro_Mini.D3_PWM, RainGauge.pin2
  N17: Arduino_Pro_Mini.D2, NRF24L01+.IRQ
  N18: BAT+.pin1, C4.1, Batt.pin1, R1.Pin_1, IC1.GND
  N19: IN+.pin1, Solar.pin2, R3.Pin_0

notes:
  +
  Meteostanica 2.2
  © Lukas Luc3as Porubcan 2016
  SCL
  SDA
  GND
  VCC
  Slovakia
  Designed in
